# Fritzing sketch Arduino_master_Reader_AVR_slave_Sender (saved by Fritzing 0.9.2b)
breadboards: 1
perfboards: 1

parts:
  パーツ1 = Arduino Uno (Rev3)
  U1 = atmega328 [package=dip]
  C1 = Ceramic Capacitor [capacitance=100nF package="100 mil [THT, multilayer]"]
  R1 = Resistor [tolerance=±5% resistance=1k package=THT]
  LED1 = LED - 5mm [color="Red (633nm)" package="5 mm [THT]"]
  R2 = Resistor [tolerance=±5% resistance=10k package=THT]
  R3 = Resistor [tolerance=±5% resistance=10k package=THT]  # not connected
  S1 = Pushbutton [package="[THT]"]
  S2 = Pushbutton [package="[THT]"]
  S3 = Pushbutton [package="[THT]"]
  S4 = Pushbutton [package="[THT]"]
  S5 = Pushbutton [package="[THT]"]
  S6 = Pushbutton [package="[THT]"]
  S7 = Pushbutton [package="[THT]"]
  S8 = Pushbutton [package="[THT]"]

nets:
  N1: パーツ1.A4/SDA, U1.A4
  N2: パーツ1.A5/SCL, U1.A5, R2.Pin_1
  N3: パーツ1.D2, U1.RESET
  5V: パーツ1.5V, U1.VCC, C1.0, R2.Pin_0
  N4: パーツ1.GND, U1.GND#7, C1.1, LED1.cathode
  N5: U1.D9_(PWM), R1.Pin_0
  N6: R1.Pin_1, LED1.anode
  N7: S1.Pin_1, S1.Pin_2
  N8: S1.Pin_3, S1.Pin_4
  N9: S2.Pin_1, S2.Pin_2
  N10: S2.Pin_3, S2.Pin_4
  N11: S3.Pin_1, S3.Pin_2
  N12: S3.Pin_3, S3.Pin_4
  N13: S4.Pin_1, S4.Pin_2
  N14: S4.Pin_3, S4.Pin_4
  N15: S5.Pin_1, S5.Pin_2
  N16: S5.Pin_3, S5.Pin_4
  N17: S6.Pin_1, S6.Pin_2
  N18: S6.Pin_3, S6.Pin_4
  N19: S7.Pin_1, S7.Pin_2
  N20: S7.Pin_3, S7.Pin_4
  N21: S8.Pin_1, S8.Pin_2
  N22: S8.Pin_3, S8.Pin_4
