# Fritzing sketch I2C_Arduino_master_AVR_slave (saved by Fritzing 0.9.2b)
breadboards: 2

parts:
  パーツ1 = Arduino Uno (Rev3)
  U1 = atmega328 [package=dip]
  C1 = Ceramic Capacitor [capacitance=100nF package="100 mil [THT, multilayer]"]
  LED1 = LED - 3mm [color="Red (633nm)" package="3 mm [THT]"]
  LED2 = LED - 3mm [color="Red (633nm)" package="3 mm [THT]"]
  LED3 = LED - 3mm [color="Red (633nm)" package="3 mm [THT]"]
  LED4 = LED - 3mm [color="Red (633nm)" package="3 mm [THT]"]
  LED5 = LED - 3mm [color="Red (633nm)" package="3 mm [THT]"]
  LED6 = LED - 3mm [color="Red (633nm)" package="3 mm [THT]"]
  LED7 = LED - 3mm [color="Red (633nm)" package="3 mm [THT]"]
  LED8 = LED - 3mm [color="Red (633nm)" package="3 mm [THT]"]
  R1 = Resistor [tolerance=±5% resistance=1k package=THT]
  R2 = Resistor [tolerance=±5% resistance=1k package=THT]
  R3 = Resistor [tolerance=±5% resistance=1k package=THT]
  R4 = Resistor [tolerance=±5% resistance=1k package=THT]
  R5 = Resistor [tolerance=±5% resistance=1k package=THT]
  R6 = Resistor [tolerance=±5% resistance=1k package=THT]
  R7 = Resistor [tolerance=±5% resistance=1k package=THT]
  R8 = Resistor [tolerance=±5% resistance=1k package=THT]
  LED9 = LED - 5mm [color="Yellow (595nm)" package="5 mm [THT]"]
  R9 = Resistor [tolerance=±5% resistance=220 package=THT]
  R10 = Resistor [tolerance=±5% resistance=10k package=THT]
  R11 = Resistor [tolerance=±5% resistance=10k package=THT]

nets:
  N1: パーツ1.A4/SDA, U1.A4, R11.Pin_1
  N2: パーツ1.A5/SCL, U1.A5, R10.Pin_1
  N3: パーツ1.GND, U1.GND#7, C1.1, LED1.cathode, LED2.cathode, LED3.cathode, LED4.cathode, LED5.cathode, LED6.cathode, LED7.cathode, LED8.cathode, LED9.cathode
  N4: パーツ1.D2, U1.RESET
  5V: パーツ1.5V, U1.VCC, C1.0, R10.Pin_0, R11.Pin_0
  N5: U1.D0_(RX), R1.Pin_1
  N6: U1.D1_(TX), R2.Pin_1
  N7: U1.D2, R3.Pin_1
  N8: U1.D3_(PWM), R4.Pin_1
  N9: U1.D4, R5.Pin_1
  N10: U1.D5_(PWM), R6.Pin_1
  N11: U1.D6_(PWM), R7.Pin_1
  N12: U1.D7, R8.Pin_1
  N13: U1.D9_(PWM), R9.Pin_1
  N14: LED1.anode, R8.Pin_0
  N15: LED2.anode, R7.Pin_0
  N16: LED3.anode, R6.Pin_0
  N17: LED4.anode, R5.Pin_0
  N18: LED5.anode, R4.Pin_0
  N19: LED6.anode, R3.Pin_0
  N20: LED7.anode, R2.Pin_0
  N21: LED8.anode, R1.Pin_0
  N22: LED9.anode, R9.Pin_0
