# Fritzing sketch I2C_Slave_Sender_ATMega88V_Byte_Sequence (saved by Fritzing 0.9.2b)
breadboards: 2
perfboards: 1

parts:
  U1 = atmega168 [package=dip]
  C1 = Ceramic Capacitor [capacitance=100nF package="100 mil [THT, multilayer]"]
  S1 = Pushbutton [package="[THT]"]
  S2 = Pushbutton [package="[THT]"]
  S3 = Pushbutton [package="[THT]"]
  S4 = Pushbutton [package="[THT]"]
  S5 = Pushbutton [package="[THT]"]
  S6 = Pushbutton [package="[THT]"]
  S7 = Pushbutton [package="[THT]"]
  S8 = Pushbutton [package="[THT]"]
  LED1 = LED - 3mm [color="Red (633nm)" package="3 mm [THT]"]
  R1 = Resistor [tolerance=±5% resistance=1k package=THT]
  R2 = Resistor [tolerance=±5% resistance=1k package=THT]
  R3 = Resistor [tolerance=±5% resistance=1k package=THT]
  R4 = Resistor [tolerance=±5% resistance=1k package=THT]
  R5 = Resistor [tolerance=±5% resistance=1k package=THT]
  R6 = Resistor [tolerance=±5% resistance=1k package=THT]
  R7 = Resistor [tolerance=±5% resistance=1k package=THT]
  R8 = Resistor [tolerance=±5% resistance=1k package=THT]
  LED2 = LED - 3mm [color="Red (633nm)" package="3 mm [THT]"]
  LED3 = LED - 3mm [color="Red (633nm)" package="3 mm [THT]"]
  LED4 = LED - 3mm [color="Red (633nm)" package="3 mm [THT]"]
  LED5 = LED - 3mm [color="Red (633nm)" package="3 mm [THT]"]
  LED6 = LED - 3mm [color="Red (633nm)" package="3 mm [THT]"]
  LED7 = LED - 3mm [color="Red (633nm)" package="3 mm [THT]"]
  LED8 = LED - 3mm [color="Red (633nm)" package="3 mm [THT]"]
  R9 = Resistor [tolerance=±5% resistance=1k package=THT]
  LED9 = LED - 3mm [color="Yellow (595nm)" package="3 mm [THT]"]
  パーツ1 = Arduino Uno (Rev3)
  R10 = Resistor [tolerance=±5% resistance=10k package=THT]
  R11 = Resistor [tolerance=±5% resistance=10k package=THT]

nets:
  N1: U1.RESET, パーツ1.D2
  VCC: U1.VCC, C1.0, パーツ1.5V, R10.Pin_0, R11.Pin_0
  N2: U1.GND#7, C1.1, LED1.cathode, LED2.cathode, LED3.cathode, LED4.cathode, LED5.cathode, LED6.cathode, LED7.cathode, LED8.cathode, LED9.cathode, パーツ1.GND
  N3: U1.XLAT1, R2.Pin_1
  N4: U1.XLAT2, R1.Pin_1
  N5: U1.D8, R8.Pin_1
  N6: U1.D9_(PWM), R7.Pin_1
  N7: U1.D10_(PWM), R6.Pin_1
  N8: U1.D11_(PWM), R5.Pin_1
  N9: U1.D12, R4.Pin_1
  N10: U1.D13, R3.Pin_1
  N11: U1.A0, R9.Pin_1
  N12: U1.A4, パーツ1.A4/SDA, R11.Pin_1
  N13: U1.A5, パーツ1.A5/SCL, R10.Pin_1
  N14: S1.Pin_1, S1.Pin_2
  N15: S1.Pin_3, S1.Pin_4
  N16: S2.Pin_1, S2.Pin_2
  N17: S2.Pin_3, S2.Pin_4
  N18: S3.Pin_1, S3.Pin_2
  N19: S3.Pin_3, S3.Pin_4
  N20: S4.Pin_1, S4.Pin_2
  N21: S4.Pin_3, S4.Pin_4
  N22: S5.Pin_1, S5.Pin_2
  N23: S5.Pin_3, S5.Pin_4
  N24: S6.Pin_1, S6.Pin_2
  N25: S6.Pin_3, S6.Pin_4
  N26: S7.Pin_1, S7.Pin_2
  N27: S7.Pin_3, S7.Pin_4
  N28: S8.Pin_1, S8.Pin_2
  N29: S8.Pin_3, S8.Pin_4
  N30: LED1.anode, R1.Pin_0
  N31: R2.Pin_0, LED2.anode
  N32: R3.Pin_0, LED3.anode
  N33: R4.Pin_0, LED4.anode
  N34: R5.Pin_0, LED5.anode
  N35: R6.Pin_0, LED6.anode
  N36: R7.Pin_0, LED7.anode
  N37: R8.Pin_0, LED8.anode
  N38: R9.Pin_0, LED9.anode
